# Fritzing sketch esp32c3mini_rgb-sensor_tcs3472_python (saved by Fritzing 0.9.9b)
circuit board: 8.46667cm x 5.64444cm
breadboards: 1

parts:
  A1 = Esp32-c3 super mini
  TCS3472 = Adafruit TCS34725 RGB Color Sensor [part_number="Adafruit #1334"]

nets:
  N1: A1.Pin_4, TCS3472.SDA
  N2: A1.Pin_5, TCS3472.SCL
  N3: A1.Pin_14, TCS3472.+3V3
  N4: A1.Pin_15, TCS3472.GND

custom parts:
  Esp32-c3 super mini: ESP32-C3 Development Board ESP32 SuperMini Development Board ESP32 Development Board WiFi Bluetooth.
  Adafruit TCS34725 RGB Color Sensor: Your electronics can now see in dazzling color with this lovely color light sensor. We found the best color sensor on the market, the TCS34725, which has RGB and Clear light sensing elements. An IR blocking filter, integrated on-chip and localized to the color sensing photodiodes, minimizes the IR spectral component of the incoming light and allows color measurements to be made accurately. The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
