# Fritzing sketch esp32wroom_rgb-sensor_tcs3472_python (saved by Fritzing 0.9.3b)
circuit board: 8.46667cm x 5.64444cm
breadboards: 2

parts:
  MH-ET_LIVE_ESP32_DEVKIT1 = MH-ET LIVE ESP32 DEVKIT 38 pins
  TCS3472 = Adafruit TCS34725 RGB Color Sensor [part_number="Adafruit #1334"]

nets:
  3V3: MH-ET_LIVE_ESP32_DEVKIT1.3V3, TCS3472.+3V3
  N1: MH-ET_LIVE_ESP32_DEVKIT1.5V, TCS3472.LED_EN
  N2: MH-ET_LIVE_ESP32_DEVKIT1.GND#64, TCS3472.GND
  N3: MH-ET_LIVE_ESP32_DEVKIT1.IO22, TCS3472.SCL
  N4: MH-ET_LIVE_ESP32_DEVKIT1.IO21, TCS3472.SDA

custom parts:
  MH-ET LIVE ESP32 DEVKIT 38 pins: http://mh.nodebb.com/topic/2/mh-et-live-esp32-devkit
  Adafruit TCS34725 RGB Color Sensor: Your electronics can now see in dazzling color with this lovely color light sensor. We found the best color sensor on the market, the TCS34725, which has RGB and Clear light sensing elements. An IR blocking filter, integrated on-chip and localized to the color sensing photodiodes, minimizes the IR spectral component of the incoming light and allows color measurements to be made accurately. The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
